# Fritzing sketch aircon board (saved by Fritzing 0.9.2b)
circuit board: 1.77688cm x 3.14345cm
breadboards: 1

parts:
  J2 = ESP01 Pin Header [form="♀ (female)" package=THT]
  Q1 = TRANSISTOR_NPN [package=to-92-ammo]
  R2 = Resistor [tolerance=±5% resistance=10k package=THT]
  R1 = Resistor [tolerance=±5% resistance=220 package=THT]
  U1 = DC-#C12Vto3v3_stepdown_converter [part_number=1102910]
  IR = LED - 5mm [color="Infrared (850nm)" package="5 mm [THT]"]
  5-12VDC = Power Jack Long holes [package=power_jack_slot]
  TX = female pin header, 1 pin [form="♀ (female)"]
  D2 = Schottky Diode [part_number=1N5817 package="300 mil [THT]"]

nets:
  N1: J2.RXD, R1.Pin_1
  VCC: J2.VCC, R2.Pin_0, U1.3v3, IR.anode
  N2: J2.GPIO0, J2.RST, J2.GPIO2, J2.CH_PD, R2.Pin_1
  GND: J2.GND, Q1.E, U1.GND
  N3: J2.TXD, TX.pin1
  N4: Q1.B, R1.Pin_0
  N5: Q1.C, IR.cathode
  N6: U1.GNDin, 5-12VDC.GNDBREAK, 5-12VDC.GND
  N7: U1.Vin, D2.cathode
  N8: 5-12VDC.PWR, D2.anode

notes:
  Aircon   Controller
  RX
  http://nightowl.space

custom parts:
  ESP01 Pin Header: Pin Header for the ESP-01 ESP8266 board
  DC-#C12Vto3v3_stepdown_converter: 12/5V to 3.3V DC-DC stepdown Voltage Regulator. Banggood product ID 1102910
  Power Jack Long holes: Power Jack This is the standard 5.5mm barrel jack for power. The PTH is the most common, proven, reliable, footprint. All others are experimental. The Slot footprint only works if the mill layer is transmitted to the PCB fab house so be warned. Spark Fun Electronics SKU : PRT-00119. Mating wall wart : TOL-00298 (and others)
