# Fritzing sketch lights_controller_pcb_2 (saved by Fritzing 0.9.2b)
circuit board: 3.73822cm x 4.10001cm
breadboards: 1

parts:
  Q1 = NPN-Transistor [package="TO92 [THT]"]
  ESP01 = ESP01 Pin Header [form="♀ (female)" package=THT]
  R1 = Resistor [tolerance=±5% resistance=220 package=THT]
  R2 = Resistor [tolerance=±5% resistance=10k package=THT]
  110-230_AC_IN = Screw terminal - 3 pins [package=THT]
  R3 = Resistor [tolerance=±5% resistance=10k package=THT]
  D2 = Schottky Diode [part_number=1N5817 package="300 mil [THT]"]
  D3 = Rectifier Diode [part_number=1N4001 package="300 mil [THT]"]
  3_3V_DC_IN = Screw terminal - 2 pins [package=THT]
  Relay1 = 3V Songle Relay [package=relay-jzc]
  110-230AC_OUT = Screw terminal - 2 pins [package=THT]
  Fuse1 = Fuse with Handler [part_number=Htc-15m]

nets:
  N1: Q1.E, R2.Pin_0
  N2: Q1.B, R1.Pin_1
  N3: Q1.C, D3.anode, Relay1.COIL1
  N4: ESP01.RXD, R1.Pin_0
  N5: ESP01.VCC, R3.Pin_0, D2.cathode, D3.cathode, Relay1.COIL2
  N6: ESP01.GPIO0, ESP01.RST, ESP01.GPIO2, ESP01.CH_PD, R3.Pin_1
  N7: ESP01.GND, R2.Pin_1, 3_3V_DC_IN.pin1
  N8: 110-230_AC_IN.L, Fuse1.Connector1
  N9: 110-230_AC_IN.N, 110-230AC_OUT.pin1
  N10: 110-230_AC_IN.S, Relay1.NO
  N11: D2.anode, 3_3V_DC_IN.pin2
  N12: Relay1.COM, 110-230AC_OUT.pin2, Fuse1.Connector2

notes:
  +
  -
  S
  N
  L
  3.3V DC
  110-230V AC
  IN
  http://nightowl.space
  OUT

custom parts:
  ESP01 Pin Header: Pin Header for the ESP-01 ESP8266 board
  Screw terminal - 3 pins: Screw terminal with 3 pins
  3V Songle Relay: SRD-0VDC-SL-C
