# Fritzing sketch rfid board rev2 (saved by Fritzing 0.9.2b)
circuit board: 6.4932cm x 4.89909cm
breadboards: 1

parts:
  R1 = Resistor [tolerance=±5% resistance=1k package=THT]
  R2 = Resistor [tolerance=±5% resistance=10k package=THT]
  D1 = Diode [package=diode-1n4148]
  D2 = Diode [package=diode-1n4148]
  J2 = NodeMCU ESP12E Right Header [form="♀ (female)" package=THT]
  J1 = NodeMCU ESP12E Left Header [form="♀ (female)" package=THT]
  Relay = 3V Songle Relay [package=relay-jzc]
  Q1 = NPN-Transistor [package="TO92 [THT]"]
  Door = Power Supply Screw Terminal v2 [package=THT]
  12V = Power Jack Long holes [package=power_jack_slot]
  RFID_RJ45 = Bel-Stewart MagJack RJ45 MFRC522 MAGJACK [package=magjack-19938]
  Fuse1 = Fuse with Handler [part_number=Htc-15m]
  Vreg = DC-#C12Vto3v3_stepdown_converter [part_number=1102910]
  D3 = Schottky Diode [part_number=1N5817 package="300 mil [THT]"]

nets:
  N1: R1.Pin_0, J2.SD3
  N2: R1.Pin_1, R2.Pin_0, Q1.B
  N3: R2.Pin_1, J2.GND#5, Q1.E
  N4: D1.A, Door.GNDin, 12V.GND, Vreg.GNDin
  N5: D1.C, Relay.NO, Door.Vin
  N6: D2.A, Relay.COIL2, Q1.C
  N7: D2.C, J2.3V3, Relay.COIL1
  N8: J1.3V3#0, Vreg.3v3
  N9: J1.GND#1, Vreg.GND#6
  N10: J1.D7, RFID_RJ45.MOSI
  N11: J1.D6, RFID_RJ45.MISO
  N12: J1.D5, RFID_RJ45.SCK
  N13: J1.GND#8, RFID_RJ45.GND, RFID_RJ45.SHIELD
  N14: J1.3V3#9, RFID_RJ45.3V3
  N15: J1.D3, RFID_RJ45.BUZ
  N16: J1.D2, RFID_RJ45.SDA
  N17: J1.D1, RFID_RJ45.RST
  N18: Relay.COM, Fuse1.Connector1
  N19: 12V.PWR, D3.anode
  N20: Fuse1.Connector2, Vreg.Vin, D3.cathode

notes:
  -
  +
  rev2
  RFID Board
  http://nightowl.space
  SDA
  SCK
  MOSI
  MISO
  BUZ
  GND
  RST
  3.3V
  D0
  D1
  D2

custom parts:
  NodeMCU ESP12E Right Header: NodeMCU ESP12E Right pin Header
  3V Songle Relay: SRD-0VDC-SL-C
  Power Supply Screw Terminal v2: Screw terminal with 2 pins for power supply
  Power Jack Long holes: Power Jack This is the standard 5.5mm barrel jack for power. The PTH is the most common, proven, reliable, footprint. All others are experimental. The Slot footprint only works if the mill layer is transmitted to the PCB fab house so be warned. Spark Fun Electronics SKU : PRT-00119. Mating wall wart : TOL-00298 (and others)
  Bel-Stewart MagJack RJ45 MFRC522 MAGJACK: RJ-45 Magjack with LEDs for MFRC522 RFID reader where pin1=>SDA and pin8=>3.3V RS Components: https://ph.rs-online.com/web/p/rj45-connectors/7418489/
  DC-#C12Vto3v3_stepdown_converter: 12/5V to 3.3V DC-DC stepdown Voltage Regulator. Banggood product ID 1102910
